# Fritzing sketch LED Signage Schematics (saved by Fritzing 0.7.11b)
breadboards: 1

parts:
  Nano1 = Arduino Nano v2.3
  Q1 = PN2907A Transistor [part_number=PN2907A package="TO92 [THT]"]
  Q2 = PN2907A Transistor [part_number=PN2907A package="TO92 [THT]"]
  R1 = 1k Ω Resistor [package=THT]
  R2 = 1k Ω Resistor [package=THT]
  R3 = 1k Ω Resistor [package=THT]
  R4 = 1k Ω Resistor [package=THT]
  R5 = 1k Ω Resistor [package=THT]
  R6 = 1k Ω Resistor [package=THT]
  R7 = 1k Ω Resistor [package=THT]
  Q3 = PN2907A Transistor [part_number=PN2907A package="TO92 [THT]"]
  Q4 = PN2907A Transistor [part_number=PN2907A package="TO92 [THT]"]
  Q5 = PN2907A Transistor [part_number=PN2907A package="TO92 [THT]"]
  Q6 = PN2907A Transistor [part_number=PN2907A package="TO92 [THT]"]
  Q8 = PN2907A Transistor [part_number=PN2907A package="TO92 [THT]"]
  Q9 = PN2907A Transistor [part_number=PN2907A package="TO92 [THT]"]
  Q10 = PN2907A Transistor [part_number=PN2907A package="TO92 [THT]"]
  Q11 = PN2907A Transistor [part_number=PN2907A package="TO92 [THT]"]
  Q12 = PN2907A Transistor [part_number=PN2907A package="TO92 [THT]"]
  Q13 = PN2907A Transistor [part_number=PN2907A package="TO92 [THT]"]
  Q14 = PN2907A Transistor [part_number=PN2907A package="TO92 [THT]"]
  Q7 = PN2907A Transistor [part_number=PN2907A package="TO92 [THT]"]
  J2 = Generic male header - 14 pins [package=THT]

nets:
  N1: Nano1.GND, J2.pin1, J2.pin2, J2.pin3
  N2: Nano1.D2, J2.pin6, J2.pin7
  N3: Nano1.D3, J2.pin4
  N4: Nano1.D5, Q10.B
  N5: Nano1.D6, Q12.B
  N6: Nano1.D7, Q14.B
  N7: Nano1.D8, Q1.B
  N8: Nano1.D9, Q4.B
  N9: Nano1.D10, Q6.B
  N10: Nano1.D11, Q8.B
  N11: Nano1.+5V, Q2.C, Q3.C, Q5.C, Q9.C, Q11.C, Q13.C, Q7.C, J2.pin5
  N12: Q1.E, Q2.E, R1.Pin_1
  N13: Q1.C, Q2.B
  N14: R1.Pin_0, J2.pin14
  N15: R2.Pin_0, J2.pin13
  N16: R2.Pin_1, Q3.E, Q4.E
  N17: R3.Pin_0, J2.pin12
  N18: R3.Pin_1, Q5.E, Q6.E
  N19: R4.Pin_0, J2.pin11
  N20: R4.Pin_1, Q8.E, Q7.E
  N21: R5.Pin_0, J2.pin10
  N22: R5.Pin_1, Q9.E, Q10.E
  N23: R6.Pin_0, J2.pin9
  N24: R6.Pin_1, Q11.E, Q12.E
  N25: R7.Pin_0, J2.pin8
  N26: R7.Pin_1, Q13.E, Q14.E
  N27: Q3.B, Q4.C
  N28: Q5.B, Q6.C
  N29: Q8.C, Q7.B
  N30: Q9.B, Q10.C
  N31: Q11.B, Q12.C
  N32: Q13.B, Q14.C

custom parts:
  PN2907A Transistor: A fairchild PNP signal transistor PN2907A
